// Logisim project FourBitParity.circ as structural Verilog: 1 circuit, main circuit implementation
module implementation (
  input  EnableIn,
  input  InputBitIn,
  input  ClkIn,
  output IsEvenOut
);

  wire and_1_out, and_2_out, and_3_out, and_4_out, and_5_out, and_6_out, and_7_out, and_8_out, and_9_out,
       demultiplexer_1_out0, demultiplexer_1_out1, demultiplexer_1_out2, demultiplexer_1_out3,
       multiplexer_2_out, nor_1_out, not_1_out, not_2_out, or_1_out, register_6_q, t0, t1, x0, x1, x2, x3,
       xnor_1_out, xnor_2_out, xor_1_out, xor_2_out;
  wire [1:0] adder_1_out, multiplexer_1_out;

  Demultiplexer #(.enable("false"), .select(2)) demultiplexer_1 (
    .out0(demultiplexer_1_out0), .out1(demultiplexer_1_out1), .out2(demultiplexer_1_out2),
    .out3(demultiplexer_1_out3), .in(InputBitIn), .sel({t1, t0}));
  Register #(.width(2)) register_1 (.D(multiplexer_1_out), .en(EnableIn), .clk(ClkIn), .Q({t1, t0}));  // open: clr
  not not_1 (not_1_out, t1);
  not not_2 (not_2_out, t0);
  and and_1 (and_1_out, t0, t1);
  nor nor_1 (nor_1_out, t0, t1);
  and and_2 (and_2_out, not_1_out, t0);
  and and_3 (and_3_out, EnableIn, and_4_out);
  and and_4 (and_4_out, not_2_out, t1);
  and and_5 (and_5_out, EnableIn, and_1_out);
  Register #(.width(1)) register_2 (.D(demultiplexer_1_out0), .en(and_6_out), .clk(ClkIn), .Q(x3));  // open: clr
  and and_6 (and_6_out, nor_1_out, EnableIn);
  and and_7 (and_7_out, and_2_out, EnableIn);
  Register #(.width(1)) register_3 (.D(demultiplexer_1_out2), .en(and_3_out), .clk(ClkIn), .Q(x1));  // open: clr
  Register #(.width(1)) register_4 (.D(demultiplexer_1_out3), .en(and_5_out), .clk(ClkIn), .Q(x0));  // open: clr
  // Probe on {t1, t0}
  Register #(.width(1)) register_5 (.D(demultiplexer_1_out1), .en(and_7_out), .clk(ClkIn), .Q(x2));  // open: clr
  Adder #(.width(2)) adder_1 (.a({t1, t0}), .b(2'b01), .out(adder_1_out));  // open: cin, cout
  Multiplexer #(.enable("false"), .width(2)) multiplexer_1 (
    .in0(2'b00), .in1(adder_1_out), .out(multiplexer_1_out), .sel(EnableIn));
  xnor xnor_1 (xnor_1_out, x3, x2);
  xnor xnor_2 (xnor_2_out, x1, x0);
  xor xor_1 (xor_1_out, x3, x2);
  xor xor_2 (xor_2_out, x1, x0);
  and and_8 (and_8_out, xnor_1_out, xnor_2_out);
  and and_9 (and_9_out, xor_1_out, xor_2_out);
  or or_1 (or_1_out, and_8_out, and_9_out);
  Multiplexer #(.enable("false"), .select(2)) multiplexer_2 (
    .in0(or_1_out), .in1(1'b0), .in2(1'b0), .in3(1'b0), .out(multiplexer_2_out), .sel({t1, t0}));
  Register #(.width(1)) register_6 (.D(1'b1), .en(EnableIn), .clk(ClkIn), .Q(register_6_q));  // open: clr
  Multiplexer #(.enable("false")) multiplexer_3 (
    .in0(1'b0), .in1(multiplexer_2_out), .out(IsEvenOut), .sel(register_6_q));

  // Other names for the same wires on the sheet: Clk = ClkIn; Enable = EnableIn; InputBit = InputBitIn;
  //   Timer[1:0] = {t1, t0}
endmodule
