// Logisim project UpDownCounter.circ as structural Verilog: 1 circuit, main circuit implementation
module implementation (
  input  EnableIn,
  input  CountUpIn,
  input  CountDownIn,
  input  clkIn,
  output [2:0] Count
);

  wire and_1_out, nor_1_out;
  wire [2:0] adder_1_out, multiplexer_1_out, multiplexer_2_out, multiplexer_3_out, subtractor_1_out;

  Register #(.width(3)) register_1 (.D(multiplexer_2_out), .en(EnableIn), .clk(clkIn), .Q(Count));  // open: clr
  Adder #(.width(3)) adder_1 (.a(Count), .b(3'b001), .out(adder_1_out));  // open: cin, cout
  and and_1 (and_1_out, Count[0], Count[1], Count[2]);
  nor nor_1 (nor_1_out, Count[0], Count[1], Count[2]);
  Multiplexer #(.enable("false"), .width(3)) multiplexer_1 (
    .in0(adder_1_out), .in1(Count), .out(multiplexer_1_out), .sel(and_1_out));
  Subtractor #(.width(3)) subtractor_1 (.a(Count), .b(3'b001), .out(subtractor_1_out));  // open: bin, bout
  Multiplexer #(.enable("false"), .select(2), .width(3)) multiplexer_2 (
    .in0(Count), .in1(multiplexer_1_out), .in2(multiplexer_3_out), .out(multiplexer_2_out),
    .sel({CountDownIn, CountUpIn}));  // open: in3
  Multiplexer #(.enable("false"), .width(3)) multiplexer_3 (
    .in0(subtractor_1_out), .in1(Count), .out(multiplexer_3_out), .sel(nor_1_out));

  // Other names for the same wires on the sheet: CountUp = CountUpIn; CountDown = CountDownIn; clk = clkIn;
  //   Enable = EnableIn

  // Notes on the sheet:
  //   mem
endmodule
